// Logisim project alu.circ as structural Verilog: 5 circuits, main circuit main
module main (
  input  [15:0] X,
  input  [15:0] Y,
  input  [3:0] switch__S,
  output signed_overflow,
  output [15:0] result,
  output equal
);

  wire comparator_1_lt;
  wire [15:0] AddOut, bc_out, bit_extender_1_out, ffo_out, op0_out, op1_out, shifter_1_out, shifter_2_out,
       shifter_3_out, SubOut, zb_out;

  assign op0_out = X & Y;  // AND_Gate op0, 16 bits wide
  assign op1_out = X | Y;  // OR_Gate op1, 16 bits wide
  Comparator #(.width(16)) comparator_1 (.a(X), .b(Y), .eq(equal), .lt(comparator_1_lt));  // open: gt
  Shifter #(.width(16)) shifter_1 (.in(X), .\dist (Y[3:0]), .out(shifter_1_out));
  Shifter #(.width(16), .shift("lr")) shifter_2 (.in(X), .\dist (Y[3:0]), .out(shifter_2_out));
  Shifter #(.width(16), .shift("ar")) shifter_3 (.in(X), .\dist (Y[3:0]), .out(shifter_3_out));
  Adder #(.width(16)) adder_1 (.a(X), .b(Y), .out(AddOut));  // open: cin, cout
  Subtractor #(.width(16)) subtractor_1 (.a(X), .b(Y), .out(SubOut));  // open: bin, bout
  ffo ffo (.X(X), .out(ffo_out));
  zb zb (.X(X), .out(zb_out));
  bc bc (.X(X), .out(bc_out));
  assign bit_extender_1_out = {{15{1'b0}}, comparator_1_lt};  // Bit_Extender bit_extender_1
  Multiplexer #(.select(4), .width(16)) multiplexer_1 (
    .in0(op0_out), .in1(op1_out), .in2(bit_extender_1_out), .in3(shifter_1_out), .in4(shifter_2_out),
    .in5(shifter_3_out), .in6(AddOut), .in7(SubOut), .in8(ffo_out), .in9(zb_out), .in10(bc_out),
    .out(result), .sel(switch__S));  // open: in11, in12, in13, in14, in15, en
  Check_Overflow Check_Overflow (
    .AddOut(AddOut), .SubOut(SubOut), .X(X), .Y(Y), .Op(switch__S), .Signed_Overflow(signed_overflow));

  // Notes on the sheet:
  //   These are INPUTS to your circuit
  //   This is an INPUT to your circuit
  //   and
  //   or
  //   slt
  //   sllv
  //   srlv
  //   srav
  //   add
  //   sub
  //   DO NOT CHANGE THE LOCATIONS OF THE INPUTS/OUTPUTS! IF YOU DO SO, YOU NEED TO MAKE SURE THE PINS ARE AT THE RIGHT PLACE!
  //   These are OUTPUTS to your circuit
endmodule

module Check_Overflow (
  input  [15:0] AddOut,
  input  [15:0] SubOut,
  input  [15:0] X,
  input  [15:0] Y,
  input  [3:0] Op,
  output Signed_Overflow
);

  wire and_1_out, and_2_out, and_3_out, and_4_out, comparator_1_eq, comparator_2_eq, not_1_out, not_2_out,
       not_3_out, not_4_out, not_5_out, not_6_out, or_1_out, or_2_out;

  not not_1 (not_1_out, X[15]);
  not not_2 (not_2_out, X[15]);
  not not_3 (not_3_out, Y[15]);
  not not_4 (not_4_out, SubOut[15]);
  not not_5 (not_5_out, Y[15]);
  not not_6 (not_6_out, AddOut[15]);
  and and_1 (and_1_out, SubOut[15], not_1_out, Y[15]);
  and and_2 (and_2_out, AddOut[15], not_2_out, not_3_out);
  and and_3 (and_3_out, not_4_out, X[15], not_5_out);
  and and_4 (and_4_out, not_6_out, X[15], Y[15]);
  Comparator #(.width(4), .mode("unsigned")) comparator_1 (.a(Op), .b(4'b0110), .eq(comparator_1_eq));  // open: gt, lt
  Comparator #(.width(4), .mode("unsigned")) comparator_2 (.a(Op), .b(4'b0111), .eq(comparator_2_eq));  // open: gt, lt
  or or_1 (or_1_out, and_1_out, and_2_out, and_3_out, and_4_out);
  or or_2 (or_2_out, comparator_1_eq, comparator_2_eq);
  Multiplexer multiplexer_1 (.in0(1'b0), .in1(or_1_out), .out(Signed_Overflow), .sel(or_2_out));  // open: en
endmodule

module ffo (
  input  [15:0] X,
  output [15:0] out
);

  wire comparator_1_eq;
  wire [3:0] bitfinder_1_index, subtractor_1_out;

  Comparator #(.width(16)) comparator_1 (.a(X), .b({16{1'b0}}), .eq(comparator_1_eq));  // open: gt, lt
  BitFinder #(.width(16), .\type ("high1")) bitfinder_1 (.in(X), .index(bitfinder_1_index));  // open: found
  Subtractor #(.width(4)) subtractor_1 (.a(4'b1111), .b(bitfinder_1_index), .out(subtractor_1_out));  // open: bin, bout
  Multiplexer #(.width(16)) multiplexer_1 (
    .in0({{12{1'b0}}, subtractor_1_out}), .in1(16'h10), .out(out), .sel(comparator_1_eq));  // open: en
endmodule

module zb (
  input  [15:0] X,
  output [15:0] out
);

  wire comparator_1_eq, comparator_2_eq;

  Comparator comparator_1 (.a(X[7:0]), .b({8{1'b0}}), .eq(comparator_1_eq));  // open: gt, lt
  Comparator comparator_2 (.a(X[15:8]), .b({8{1'b0}}), .eq(comparator_2_eq));  // open: gt, lt
  or or_1 (out[0], comparator_1_eq, comparator_2_eq);

  assign out[15:1] = {15{1'b0}};
endmodule

module bc (
  input  [15:0] X,
  output [15:0] out
);

  BitAdder #(.width(1)) bitadder_1 (
    .in0(X[0]), .in1(X[1]), .in2(X[2]), .in3(X[3]), .in4(X[4]), .in5(X[5]), .in6(X[6]), .in7(X[7]),
    .in8(X[8]), .in9(X[9]), .in10(X[10]), .in11(X[11]), .in12(X[12]), .in13(X[13]), .in14(X[14]),
    .in15(X[15]), .out(out[4:0]));

  assign out[15:5] = {11{1'b0}};
endmodule
