// Logisim project cpu.circ as structural Verilog: 5 circuits, main circuit main
module main (
  input  [15:0] From_Instr_Mem,
  input  clk,
  output [15:0] r0,
  output [15:0] r1,
  output [15:0] r2,
  output [15:0] r3,
  output [15:0] Display_0,
  output [15:0] Display_1,
  output [15:0] To_Instr_Mem,
  output [15:0] Data_Mem_Data,
  output [15:0] Data_Mem_Addr,
  output Data_Mem_Write
);

  wire ALU_signed_overflow, ALUSrc, and_2_out, and_3_out, and_4_out, and_5_out, BEQ, BNE, BranchTaken,
       comparator_1_eq, comparator_2_eq, Disp, Eq, Jal, Jr, Jump, LUI, MemRead, MemtoReg, not_1_out,
       or_2_out, RegDst, RegWrite, Signed;
  wire [1:0] multiplexer_5_out, multiplexer_6_out;
  wire [3:0] alu_control_1_out_3, ALUOp;
  wire [15:0] adder_1_out, adder_2_out, and_1_out, bit_extender_1_out, bit_extender_2_out,
       bit_extender_3_out, imm, multiplexer_1_out, multiplexer_2_out, multiplexer_3_out, multiplexer_4_out,
       multiplexer_8_out, multiplexer_9_out, multiplexer_10_out, multiplexer_11_out, multiplexer_12_out,
       multiplexer_13_out, multiplexer_14_out, or_1_out, PC, Reg_read_data_2, register_2_q, rs;

  Multiplexer #(.width(16)) multiplexer_1 (
    .in0(multiplexer_2_out), .in1(rs), .out(multiplexer_1_out), .sel(Jr));  // open: en
  Register #(.width(16)) u_PC (.D(multiplexer_1_out), .Q(PC), .clk(clk));  // open: en, clr
  Register #(.width(16)) register_1 (.D(multiplexer_1_out), .Q(To_Instr_Mem), .clk(clk));  // open: en, clr
  Multiplexer #(.width(16)) multiplexer_2 (
    .in0(multiplexer_3_out), .in1(or_1_out), .out(multiplexer_2_out), .sel(Jump));  // open: en
  assign and_1_out = 16'hf000 & PC;  // AND_Gate and_1, 16 bits wide
  Multiplexer #(.width(16)) multiplexer_3 (
    .in0(multiplexer_13_out), .in1(or_1_out), .out(multiplexer_3_out), .sel(Jal));  // open: en
  assign or_1_out = and_1_out | bit_extender_1_out;  // OR_Gate or_1, 16 bits wide
  Multiplexer #(.width(16)) multiplexer_4 (
    .in0(From_Instr_Mem), .in1({16{1'b0}}), .out(multiplexer_4_out), .sel(or_2_out));  // open: en
  or or_2 (or_2_out, BranchTaken, Jal, Jump, Jr);
  assign bit_extender_1_out = {{4{1'b0}}, register_2_q[11:0]};  // Bit_Extender bit_extender_1
  Register #(.width(16)) register_2 (.D(multiplexer_4_out), .Q(register_2_q), .clk(clk));  // open: en, clr
  Control Control (
    .op(register_2_q[15:12]), .RegDst(RegDst), .RegWrite(RegWrite), .MemWrite(Data_Mem_Write),
    .MemRead(MemRead), .MemtoReg(MemtoReg), .ALUOp(ALUOp), .ALUSrc(ALUSrc), .Jal(Jal), .J(Jump), .Jr(Jr),
    .Beq(BEQ), .Bne(BNE), .Lui(LUI), .Disp(Disp), .SignedExt(Signed));
  Multiplexer #(.width(2)) multiplexer_5 (
    .in0(register_2_q[9:8]), .in1(register_2_q[7:6]), .out(multiplexer_5_out), .sel(RegDst));  // open: en
  Multiplexer #(.width(2)) multiplexer_6 (
    .in0(multiplexer_5_out), .in1(2'b11), .out(multiplexer_6_out), .sel(Jal));  // open: en
  assign bit_extender_2_out = {{8{1'b0}}, register_2_q[7:0]};  // Bit_Extender bit_extender_2
  Multiplexer #(.width(16)) multiplexer_7 (
    .in0(bit_extender_2_out), .in1(bit_extender_3_out), .out(imm), .sel(Signed));  // open: en
  assign bit_extender_3_out = {{8{register_2_q[7]}}, register_2_q[7:0]};  // Bit_Extender bit_extender_3
  Adder #(.width(16)) adder_1 (.a(16'h1), .b(PC), .out(adder_1_out));  // open: cin, cout
  Regfile_main Reg (
    .Read_register_1(register_2_q[11:10]), .Read_register_2(register_2_q[9:8]),
    .write_register(multiplexer_6_out), .write_data(multiplexer_8_out), .Reg_0_Value(r0), .Reg_1_Value(r1),
    .Reg_2_Value(r2), .Reg_3_Value(r3), .RegWrite(RegWrite), .clock(clk), .Read_Data_1(rs),
    .Read_Data_2(Reg_read_data_2));
  Multiplexer #(.width(16)) multiplexer_8 (
    .in0(multiplexer_14_out), .in1(PC), .out(multiplexer_8_out), .sel(Jal));  // open: en
  Adder #(.width(16)) adder_2 (.a(PC), .b(imm), .out(adder_2_out));  // open: cin, cout
  Multiplexer #(.width(16)) multiplexer_9 (.in0(rs), .in1(imm), .out(multiplexer_9_out), .sel(LUI));  // open: en
  Multiplexer #(.width(16)) multiplexer_10 (
    .in0(Reg_read_data_2), .in1(imm), .out(multiplexer_10_out), .sel(ALUSrc));  // open: en
  Multiplexer #(.width(16)) multiplexer_11 (
    .in0(adder_1_out), .in1(adder_2_out), .out(multiplexer_11_out), .sel(and_2_out));  // open: en
  and and_2 (and_2_out, BNE, not_1_out);
  not not_1 (not_1_out, Eq);
  alu_main ALU (
    .switch__S(alu_control_1_out_3), .X(multiplexer_9_out), .equal(Eq), .result(Data_Mem_Addr),
    .signed_overflow(ALU_signed_overflow), .Y(multiplexer_12_out));
  Multiplexer #(.width(16)) multiplexer_12 (
    .in0(multiplexer_10_out), .in1(16'h8), .out(multiplexer_12_out), .sel(LUI));  // open: en
  ALU_Control alu_control_1 (.Function(register_2_q[3:0]), .ALUOp(ALUOp), .out_3(alu_control_1_out_3));
  Multiplexer #(.width(16)) multiplexer_13 (
    .in0(multiplexer_11_out), .in1(adder_2_out), .out(multiplexer_13_out), .sel(and_3_out));  // open: en
  and and_3 (and_3_out, BEQ, Eq);
  // Probe on Data_Mem_Addr
  LED led_1 (.in(ALU_signed_overflow));
  or or_3 (BranchTaken, and_2_out, and_3_out);
  Memory memory_1 (
    .DataIn(Reg_read_data_2), .Address(Data_Mem_Addr), .clk(clk), .MemWrite(Data_Mem_Write),
    .DataOut(Data_Mem_Data));  // open: MemRead
  Multiplexer #(.width(16)) multiplexer_14 (
    .in0(Data_Mem_Addr), .in1(Data_Mem_Data), .out(multiplexer_14_out), .sel(MemtoReg));  // open: en
  Comparator #(.width(16)) comparator_1 (.a(imm), .b({16{1'b0}}), .eq(comparator_1_eq));  // open: gt, lt
  Comparator #(.width(16)) comparator_2 (.a(imm), .b(16'h1), .eq(comparator_2_eq));  // open: gt, lt
  Hex_Digit_Display hex_digit_display_1 (.value(Display_0[15:12]));  // open: dp
  and and_4 (and_4_out, comparator_1_eq, Disp);
  Hex_Digit_Display hex_digit_display_2 (.value(Display_1[15:12]));  // open: dp
  and and_5 (and_5_out, comparator_2_eq, Disp);
  Hex_Digit_Display hex_digit_display_3 (.value(Display_0[11:8]));  // open: dp
  Hex_Digit_Display hex_digit_display_4 (.value(Display_0[7:4]));  // open: dp
  Register #(.width(16)) register_3 (.D(rs), .en(and_4_out), .Q(Display_0), .clk(clk));  // open: clr
  Hex_Digit_Display hex_digit_display_5 (.value(Display_1[7:4]));  // open: dp
  Hex_Digit_Display hex_digit_display_6 (.value(Display_1[11:8]));  // open: dp
  Register #(.width(16)) register_4 (.D(rs), .en(and_5_out), .Q(Display_1), .clk(clk));  // open: clr
  Hex_Digit_Display hex_digit_display_7 (.value(Display_0[3:0]));  // open: dp
  Hex_Digit_Display hex_digit_display_8 (.value(Display_1[3:0]));  // open: dp

  // Other names for the same wires on the sheet: C = clk; d0[15:0] = Display_0; d1[15:0] = Display_1;
  //   MemWrite = Data_Mem_Write

  // Notes on the sheet:
  //   This is the current PC that you need to send as OUTPUT
  //   This is the instruction that you would receive as INPUT
  //   This is a CLK that is an INPUT driven from the harness.
  //   Remember, this circuit is loaded from the harness to be tested!
  //   DO NOT CHANGE THE LOCATIONS OF THE INPUTS/OUTPUTS! IF YOU DO SO, YOU NEED TO MAKE SURE THE PINS ARE AT THE RIGHT PLACE!
  //   These are OUTPUTS to the circuit
  //   These are OUTPUTS to the circuit
endmodule

module SignedExt (
  input  [7:0] Input,
  output [15:0] Output
);

  wire comparator_1_eq;

  // Probe on Input
  Multiplexer #(.width(8)) multiplexer_1 (
    .in0({8{1'b0}}), .in1({8{1'b1}}), .out(Output[15:8]), .sel(comparator_1_eq));  // open: en
  Comparator #(.width(1), .mode("unsigned")) comparator_1 (
    .a(Input[7]), .b(1'b1), .eq(comparator_1_eq));  // open: gt, lt
  // Probe on {Output[15:8], Input}

  assign Output[7:0] = Input;
endmodule

module Memory (
  input  MemRead,
  input  [15:0] DataIn,
  input  [15:0] Address,
  input  clk,
  input  MemWrite,
  output [15:0] DataOut
);

  wire not_1_out;

  assign DataOut = MemWrite ? DataIn : 16'bz;  // Controlled_Buffer controlled_buffer_1
  not not_1 (not_1_out, MemWrite);
  RAM #(.addrWidth(16), .dataWidth(16)) ram_1 (
    .addr(Address), .data(DataOut), .sel(1'b1), .clk(clk), .ld(not_1_out));  // open: clr

  // Notes on the sheet:
  //   MemRead/Write
endmodule

module Control (
  input  [3:0] op,
  output RegDst,
  output RegWrite,
  output MemWrite,
  output MemRead,
  output MemtoReg,
  output [3:0] ALUOp,
  output ALUSrc,
  output Jal,
  output J,
  output Jr,
  output Beq,
  output Bne,
  output Lui,
  output Disp,
  output SignedExt
);

  wire _1, _2, _3, _4, _5, _6;

  Decoder #(.select(4), .enable("false")) decoder_1 (
    .out0(RegDst), .out1(_1), .out2(_2), .out3(_3), .out4(_4), .out5(_5), .out6(_6), .out7(Jal), .out8(J),
    .out9(Jr), .out10(Beq), .out11(Bne), .out12(MemWrite), .out13(Lui), .out14(MemRead), .out15(Disp),
    .sel(op));
  or or_1 (RegWrite, RegDst, _1, _2, _3, _4, _5, _6, Jal, Lui, MemRead);
  or or_2 (ALUSrc, _4, _5, _6, MemWrite, Lui, MemRead);
  or or_3 (SignedExt, _4, Beq, Bne, MemWrite, MemRead);

  assign ALUOp = op;
  assign MemtoReg = MemRead;

  // Other names for the same wires on the sheet: _0 = RegDst; _7 = Jal; _8 = J; _9 = Jr; _10 = Beq; _11 = Bne;
  //   _12 = MemWrite; _13 = Lui; _14 = MemRead; _15 = Disp
endmodule

module ALU_Control (
  input  [3:0] Function,
  input  [3:0] ALUOp,
  output [3:0] out_3
);

  Multiplexer #(.select(4), .width(4)) multiplexer_1 (
    .in0(Function), .in1(4'b1000), .in2(4'b1001), .in3(4'b1010), .in4(4'b0110), .in5(4'b0000), .in6(4'b0001),
    .in12(4'b0110), .in13(4'b0011), .in14(4'b0110), .out(out_3), .sel(ALUOp));  // open: in7, in8, in9, in10, in11, in15, en
endmodule
